# Fritzing sketch modeloEsqematicoAtmega382 (saved by Fritzing 0.9.3b)
circuit board: 2.34752cm x 4.37333cm
breadboards: 2

parts:
  ZS-042_RTC1 = ZS-042 RTC Module
  R1 = Resistor [tolerance=±5% resistance=4.70 package="0805 [SMD]"]
  R2 = Resistor [tolerance=±5% resistance=4.70 package="0805 [SMD]"]
  R3 = Resistor [tolerance=±5% resistance=4.70 package="0805 [SMD]"]
  R5 = Resistor [tolerance=±5% resistance=4.70 package="0805 [SMD]"]
  DS2 = DS18B20 1-Wire Temperature Sensor [part_number=DS18B20]
  U1 = FS1000A - 433Mhz RF Transmitter [package=THT]
  U3 = atmega328 [package=dip]
  U4 = atmega328 [package=dip]
  Componente2 = Adafruit MicroSD card breakout board [part_number="Adafruit #254"]
  U2 = XD-RF-5V [package=THT]

nets:
  GND: ZS-042_RTC1.GND, U4.GND, Componente2.GND, U2.GND
  VCC: ZS-042_RTC1.VCC, U4.VCC, Componente2.VCC, U2.VCC
  N1: ZS-042_RTC1.SDA, U4.A4
  N2: ZS-042_RTC1.SCL, U4.A5
  N3: R1.Pin_0, Componente2.CLK
  N4: R1.Pin_1, U4.D13
  N5: R2.Pin_0, Componente2.DI
  N6: R2.Pin_1, U4.D11_(PWM)
  N7: R3.Pin_0, U4.D4
  N8: R3.Pin_1, Componente2.CS
  N9: R5.Pin_0, DS2.DQ, U3.D2
  VCC_2: R5.Pin_1, DS2.VDD, U1.VCC, U1.Antenna, U3.VCC
  GND_2: DS2.GND, U1.GND, U3.GND
  N10: U1.DATA, U3.D12
  N11: U4.D5_(PWM), U2.DATA#2
  N12: U4.D12, Componente2.DO

custom parts:
  FS1000A - 433Mhz RF Transmitter: This is 433Mhz RF transmitter with receiver kit for Arduino ARM MCU wireless Application environment: Remote control switch, receiver module, motorcycles, automobile anti-theft products, home security products, electric doors, shutter doors, windows, remote control socket, remote control LED, remote audio remote control electric doors, garage door remote control, remote control retractable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
  Adafruit MicroSD card breakout board: Not just a simple breakout board, this microSD adapter goes the extra mile - designed for ease of use. Onboard 5v->3v regulator provides 150mA for power-hungry cards 3v level shifting means you can use this with ease on either 3v or 5v systems Uses a proper level shifting chip, not resistors: less problems, and faster read/write access Use 3 or 4 digital pins to read and write 2Gb+ of storage!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
  XD-RF-5V: This is 433Mhz RF transmitter with receiver kit for Arduino ARM MCU wireless Application environment: Remote control switch, receiver module, motorcycles, automobile anti-theft products, home security products, electric doors, shutter doors, windows, remote control socket, remote control LED, remote audio remote control electric doors, garage door remote control, remote control retractable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
